// Logisim project PB1204microcode.circ as structural Verilog: 1 circuit, main circuit main
module main (
  input  [3:0] DATA,
  input  [3:0] RegisterNumber,
  input  [3:0] FunctionNumber,
  input  in_4,
  input  in_5,
  input  in_6,
  input  in_7,
  input  in_8
);

  wire and_1_out, and_2_out, and_3_out, and_4_out, and_5_out, and_6_out, and_7_out, ARegisterEnable,
       clock_1_out, DecrementRegister, IncrementRegister, or_1_out, or_2_out, or_3_out, or_4_out, PC00_carry,
       PC0Enable, PC01_carry, PC1Enable, PC2Enable, ReadFromDatabus, s_r_ff_1_q, TriggerUpdateOfRegister,
       undriven, WriteToAddressRegister, WriteToDatabus;
  wire [3:0] AData, BufferData, DATABUS, PC0Data, PC1Data, PC2Data;

  Register #(.width(4)) BufferRegister (.D(DATABUS), .en(in_5), .clk(in_4), .Q(BufferData));  // open: clr
  and and_1 (and_1_out, PC1Enable, WriteToDatabus);
  and and_2 (and_2_out, PC0Enable, WriteToDatabus);
  and and_3 (and_3_out, ARegisterEnable, WriteToDatabus);
  assign DATABUS = and_3_out ? AData : 4'bz;  // Controlled_Buffer controlled_buffer_1
  assign DATABUS = and_2_out ? PC0Data : 4'bz;  // Controlled_Buffer controlled_buffer_2
  Controlled_Buffer #(.width(4)) controlled_buffer_3 (.in(PC1Data), .en(and_1_out));  // open: out
  Register #(.width(4)) ARegister (
    .D(BufferData), .en(ARegisterEnable), .clk(TriggerUpdateOfRegister), .Q(AData));  // open: clr
  S_R_Flip_Flop HasBitmaskBeenSet ();  // open: S, R, clk, Q, reset, Qn, preset
  Register #(.width(12)) BitmaskRegister ();  // open: D, en, clk, Q, clr
  Demultiplexer #(.select(4)) demultiplexer_1 (
    .out8(ARegisterEnable), .out9(PC0Enable), .out10(PC1Enable), .out11(PC2Enable), .in(in_8),
    .sel(RegisterNumber));  // open: out0, out1, out2, out3, out4, out5, out6, out7, out12, out13, out14, out15
  Clock clock_1 (.out(clock_1_out));
  Demultiplexer #(.select(4)) demultiplexer_2 (
    .out0(ReadFromDatabus), .out1(WriteToDatabus), .out2(WriteToAddressRegister),
    .out3(TriggerUpdateOfRegister), .out4(IncrementRegister), .out5(DecrementRegister), .in(clock_1_out),
    .sel(FunctionNumber));  // open: out6, out7, out8, out9, out10, out11, out12, out13, out14, out15
  S_R_Flip_Flop s_r_ff_1 (
    .S(IncrementRegister), .R(DecrementRegister), .Q(s_r_ff_1_q));  // open: clk, reset, Qn, preset
  buf or_1 (or_1_out, s_r_ff_1_q);  // OR_Gate
  and and_4 (and_4_out, PC2Enable, TriggerUpdateOfRegister);
  and and_5 (and_5_out, PC1Enable, TriggerUpdateOfRegister);
  and and_6 (and_6_out, PC0Enable, TriggerUpdateOfRegister);
  and and_7 (and_7_out, PC0Enable, or_1_out);
  or or_2 (or_2_out, and_4_out, PC01_carry);
  or or_3 (or_3_out, and_5_out, PC00_carry);
  or or_4 (or_4_out, and_6_out, and_7_out, in_7);
  Counter #(.max('hf), .width(4)) PC02 (
    .load(and_4_out), .up(undriven), .count(1'b1), .clk(or_2_out), .D(BufferData), .Q(PC2Data));  // open: clr, carry
  Counter #(.max('hf), .width(4)) PC01 (
    .load(and_5_out), .up(undriven), .count(1'b1), .clk(or_3_out), .D(BufferData), .carry(PC01_carry),
    .Q(PC1Data));  // open: clr
  Counter #(.max('hf), .width(4)) PC00 (
    .load(and_6_out), .up(s_r_ff_1_q), .count(1'b1), .clk(or_4_out), .D(BufferData), .carry(PC00_carry),
    .Q(PC0Data));  // open: clr

  // Other names for the same wires on the sheet: FuncID[3:0] = FunctionNumber; IncDec = in_6; LoadMode = in_5;
  //   RegID[3:0] = RegisterNumber
endmodule
