// Logisim project PBP1204.circ as structural Verilog: 1 circuit, main circuit main
module main (
  input  ManualMode,
  input  [3:0] Action,
  input  [3:0] Location
);

  wire AAD, adder_1_cout, ANA, and_1_out, and_2_out, and_4_out, and_5_out, and_6_out, and_7_out, and_8_out,
       and_9_out, and_10_out, and_11_out, and_12_out, and_13_out, and_14_out, and_15_out, and_16_out,
       and_17_out, and_18_out, and_19_out, and_20_out, ANO, ANT, ARenable, ASL, ASR, BMenable, BMset,
       BRenable, CarryFlag_q, CLK, clock_2_out, comparator_1_lt, comparator_2_eq, comparator_3_eq, CTF,
       CycleFinished, DEC, demultiplexer_2_out15, demultiplexer_3_out8, demultiplexer_3_out9,
       demultiplexer_3_out10, demultiplexer_3_out12, demultiplexer_3_out13, demultiplexer_3_out14, HBenable,
       HPCenable, HSPenable, INC, INTenable, IRenable, LBenable, LPCenable, LSPenable, MBenable, MPCenable,
       MSPenable, not_1_out, not_2_out, not_3_out, not_4_out, not_5_out, not_6_out, not_8_out, or_3_out,
       or_4_out, or_6_out, or_7_out, or_8_out, or_9_out, or_10_out, pull_resistor_4_node, RBR, RDB, Read,
       RESET, RRD, ShortWideInst, TFenable, UAR, UBM, WBR, WDB;
  wire [3:0] ALUresult, AReg, BitmaskReg, BReg, controlled_buffer_6_out, DATA, HiBuffer_q,
       InstructionRegister_q, LowBuffer_q, MidBuffer_q, pull_resistor_3_node, rom_1_data;
  wire [4:0] InstructionCounter_q;
  wire [7:0] controlled_buffer_2_out, Microcode_data;
  wire [9:9] and_3_out;
  wire [11:0] ADDRESS, AddressBuffer, controlled_buffer_14_out, ProgramCounter, StackPointer;

  and and_1 (and_1_out, RRD, IRenable);
  or or_1 (Read, UBM, RDB);
  or or_2 (CycleFinished, and_1_out, RESET);
  // LedBar #(.inputtype("row"), .matrixcols(12)) ledbar_1: pin names not known; wires that end beside it: ADDRESS
  // LedBar #(.inputtype("row"), .matrixcols(4)) ledbar_2: pin names not known; wires that end beside it: DATA
  Clock clock_1 (.out(CLK));
  POR por_1 (.out(RESET));
  // LedBar #(.inputtype("row"), .matrixcols(4)) ledbar_3: pin names not known; wires that end beside it: {Read, WDB, RESET, CLK}
  Counter #(.max('h1f), .trigger("falling"), .width(5)) InstructionCounter (
    .clr(CycleFinished), .load(1'b0), .up(1'b1), .count(1'b1), .clk(CLK), .Q(InstructionCounter_q));  // open: D, carry
  Register #(.trigger("falling"), .width(4)) InstructionRegister (
    .D(DATA), .en(IRenable), .clk(CLK), .Q(InstructionRegister_q), .clr(CycleFinished));
  Pull_Resistor pull_resistor_1 (.node(DATA));
  Pull_Resistor pull_resistor_2 (.node(ADDRESS));
  Comparator #(.mode("unsigned"), .width(4)) comparator_1 (
    .a(InstructionRegister_q), .b(4'b0101), .lt(comparator_1_lt));  // open: gt, eq
  and and_2 (and_2_out, CLK, ADDRESS[11]);
  ROM #(.addrWidth(10)) Microcode (
    .addr({and_3_out[9], InstructionRegister_q, InstructionCounter_q}), .data(Microcode_data));
  and and_3 (and_3_out[9], ShortWideInst, comparator_1_lt);
  RAM #(.addrWidth(11), .dataWidth(4), .databus("bidir")) ram_1 (
    .addr(ADDRESS[10:0]), .we(WDB), .oe(Read), .clk(and_2_out), .data(DATA));
  ROM #(.addrWidth(11), .dataWidth(4)) rom_1 (.addr(ADDRESS[10:0]), .data(rom_1_data));
  Hex_Digit_Display #(.decimalPoint("false")) A (.value(AReg));
  // LedBar #(.inputtype("row"), .matrixcols(4)) ledbar_4: pin names not known
  // LedBar #(.inputtype("row"), .matrixcols(4)) ledbar_5: pin names not known
  // LedBar #(.inputtype("row"), .matrixcols(12)) ledbar_6: pin names not known; wires that end beside it: ProgramCounter
  // LedBar #(.inputtype("row"), .matrixcols(12)) ledbar_7: pin names not known; wires that end beside it: StackPointer
  Hex_Digit_Display #(.decimalPoint("false")) B (.value(BReg));
  not not_1 (not_1_out, ADDRESS[11]);
  and and_4 (and_4_out, not_1_out, Read);
  assign DATA = and_4_out ? rom_1_data : 4'bz;  // Controlled_Buffer controlled_buffer_1
  assign controlled_buffer_2_out = ManualMode ? {Location, Action} : 8'bz;  // Controlled_Buffer controlled_buffer_2
  not not_2 (not_2_out, ManualMode);
  assign controlled_buffer_2_out = not_2_out ? Microcode_data : 8'bz;  // Controlled_Buffer controlled_buffer_3
  Demultiplexer #(.select(4)) demultiplexer_1 (
    .out0(RDB), .out1(WDB), .out2(RBR), .out3(WBR), .out4(UBM), .out5(UAR), .out6(CTF), .out7(RRD),
    .out8(ANA), .out9(ANO), .out10(ANT), .out11(AAD), .out12(ASL), .out13(ASR), .out14(INC), .out15(DEC),
    .in(CLK), .sel(controlled_buffer_2_out[3:0]));
  Demultiplexer #(.select(4)) demultiplexer_2 (
    .out0(IRenable), .out1(LBenable), .out2(MBenable), .out3(HBenable), .out4(ARenable), .out5(BRenable),
    .out6(TFenable), .out7(BMenable), .out8(LPCenable), .out9(MPCenable), .out10(HPCenable),
    .out11(INTenable), .out12(LSPenable), .out13(MSPenable), .out14(HSPenable),
    .out15(demultiplexer_2_out15), .in(CLK), .sel(pull_resistor_3_node));
  Pull_Resistor pull_resistor_3 (.node(pull_resistor_3_node));
  assign pull_resistor_3_node = not_3_out ? controlled_buffer_2_out[7:4] : 4'bz;  // Controlled_Buffer controlled_buffer_4
  not not_3 (not_3_out, comparator_2_eq);
  Comparator #(.mode("unsigned"), .width(4)) comparator_2 (
    .a(controlled_buffer_2_out[7:4]), .b(4'b1111), .eq(comparator_2_eq));  // open: gt, lt
  assign pull_resistor_3_node = comparator_2_eq ? BitmaskReg : 4'bz;  // Controlled_Buffer controlled_buffer_5
  assign controlled_buffer_6_out = AAD ? ALUresult : 4'bz;  // Controlled_Buffer controlled_buffer_6
  assign controlled_buffer_6_out = RDB ? DATA : 4'bz;  // Controlled_Buffer controlled_buffer_7
  and and_5 (and_5_out, ARenable, WBR);
  assign controlled_buffer_6_out = and_5_out ? AReg : 4'bz;  // Controlled_Buffer controlled_buffer_8
  and and_6 (and_6_out, BRenable, WBR);
  assign controlled_buffer_6_out = and_6_out ? BReg : 4'bz;  // Controlled_Buffer controlled_buffer_9
  and and_7 (and_7_out, CLK, BMenable);
  or or_3 (or_3_out, and_6_out, LBenable, and_5_out);
  or or_4 (or_4_out, RESET, CycleFinished);
  Counter #(.max('hf), .trigger("falling"), .width(4)) BitmaskRegister (
    .clr(or_4_out), .load(not_4_out), .up(pull_resistor_4_node), .count(INC), .clk(and_7_out), .D(DATA),
    .Q(BitmaskReg));  // open: carry
  not not_4 (not_4_out, INC);
  Pull_Resistor #(.pull(1)) pull_resistor_4 (.node(pull_resistor_4_node));
  Register #(.trigger("falling"), .width(4)) LowBuffer (
    .D(controlled_buffer_6_out), .en(or_3_out), .clk(CLK), .Q(LowBuffer_q), .clr(RESET));
  Register #(.trigger("falling"), .width(4)) MidBuffer (
    .D(controlled_buffer_6_out), .en(MBenable), .clk(CLK), .Q(MidBuffer_q), .clr(RESET));
  Register #(.trigger("falling"), .width(4)) HiBuffer (
    .D(controlled_buffer_6_out), .en(HBenable), .clk(CLK), .Q(HiBuffer_q), .clr(RESET));
  assign AddressBuffer[3:0] = INC ? BReg : 4'bz;  // Controlled_Buffer controlled_buffer_10
  assign AddressBuffer[3:0] = RBR ? LowBuffer_q : 4'bz;  // Controlled_Buffer controlled_buffer_11
  assign AddressBuffer[7:4] = RBR ? MidBuffer_q : 4'bz;  // Controlled_Buffer controlled_buffer_12
  assign AddressBuffer[11:8] = RBR ? HiBuffer_q : 4'bz;  // Controlled_Buffer controlled_buffer_13
  Demultiplexer #(.select(4)) demultiplexer_3 (
    .out8(demultiplexer_3_out8), .out9(demultiplexer_3_out9), .out10(demultiplexer_3_out10),
    .out12(demultiplexer_3_out12), .out13(demultiplexer_3_out13), .out14(demultiplexer_3_out14), .in(1'b1),
    .sel(BitmaskReg));  // open: out0, out1, out2, out3, out4, out5, out6, out7, out11, out15
  not not_5 (not_5_out, WBR);
  not not_6 (not_6_out, WBR);
  or or_5 (ShortWideInst, demultiplexer_3_out8, demultiplexer_3_out9, demultiplexer_3_out10, demultiplexer_3_out12, demultiplexer_3_out13, demultiplexer_3_out14);
  not not_7 (BMset, comparator_3_eq);
  Comparator #(.mode("unsigned"), .width(4)) comparator_3 (
    .a(BitmaskReg), .b(4'b1111), .eq(comparator_3_eq));  // open: gt, lt
  and and_8 (and_8_out, not_5_out, ARenable);
  and and_9 (and_9_out, ARenable, RRD);
  or or_6 (or_6_out, and_9_out, RESET);
  and and_10 (and_10_out, not_6_out, BRenable);
  and and_11 (and_11_out, BRenable, RRD);
  Clock clock_2 (.out(clock_2_out));
  Register #(.trigger("falling"), .width(4)) ARegister (
    .D(AddressBuffer[3:0]), .en(and_8_out), .clk(CLK), .Q(AReg), .clr(or_6_out));
  or or_7 (or_7_out, and_11_out, RESET);
  Adder #(.width(4)) adder_1 (.a(AReg), .b(BReg), .out(ALUresult), .cin(CarryFlag_q), .cout(adder_1_cout));
  D_Flip_Flop CarryFlag (.D(adder_1_cout), .clk(and_12_out), .Q(CarryFlag_q), .reset(RESET));  // open: Qn, preset
  and and_12 (and_12_out, AAD, clock_2_out);
  Register #(.trigger("falling"), .width(4)) BRegister (
    .D(AddressBuffer[3:0]), .en(and_10_out), .clk(CLK), .Q(BReg), .clr(or_7_out));
  D_Flip_Flop ParityFlag ();  // open: D, clk, Q, Qn, preset, reset
  D_Flip_Flop BorrowFlag ();  // open: D, clk, Q, Qn, preset, reset
  or or_8 (or_8_out, INC, DEC);
  and and_13 (and_13_out, RBR, HPCenable);
  and and_14 (and_14_out, INC, CLK);
  and and_15 (and_15_out, CLK, and_13_out);
  and and_16 (and_16_out, or_8_out, CLK);
  and and_17 (and_17_out, CLK, and_18_out);
  or or_9 (or_9_out, and_14_out, and_15_out);
  and and_18 (and_18_out, RBR, HSPenable);
  not not_8 (not_8_out, DEC);
  or or_10 (or_10_out, and_16_out, and_17_out);
  Counter #(.max('hfff), .trigger("falling"), .width(12)) u_ProgramCounter (
    .clr(RESET), .load(and_13_out), .up(1'b1), .count(LPCenable), .clk(or_9_out), .D(AddressBuffer),
    .Q(ProgramCounter));  // open: carry
  Counter #(.max('hfff), .trigger("falling"), .width(12)) u_StackPointer (
    .clr(RESET), .load(and_18_out), .up(not_8_out), .count(LSPenable), .clk(or_10_out), .D(AddressBuffer),
    .Q(StackPointer));  // open: carry
  and and_19 (and_19_out, LPCenable, UAR);
  and and_20 (and_20_out, LSPenable, UAR);
  assign controlled_buffer_14_out = and_19_out ? ProgramCounter : 12'bz;  // Controlled_Buffer controlled_buffer_14
  assign controlled_buffer_14_out = and_20_out ? StackPointer : 12'bz;  // Controlled_Buffer controlled_buffer_15
  Register #(.trigger("falling"), .width(12)) u_AddressBuffer (
    .D(controlled_buffer_14_out), .en(UAR), .clk(CLK), .Q(ADDRESS), .clr(RESET));

  // Other names for the same wires on the sheet: Write = WDB

  // Notes on the sheet:
  //   Check if Bitmask is needed
  //   contents of Microcode (hex, n*v repeats v):
  //   0 8e 85 70 8e 85 10 f2 8e 85 7 342*0 1b 42 8e 85 7 91*0 43 4e 52 8e 85 7 61*0 8e 85 10 7e 8e 85 20
  //   7e 8e 85 30 f2 85 7
  //   contents of rom_1 (hex, n*v repeats v):
  //   0 4 0 0 5 1 b e 0 8 6
  //   Action
  //   Location
  //   Hack to make SWP work!
endmodule
